// Logisim project Lab2_PartA_forPartC_Casper.circ as structural Verilog: 2 circuits, main circuit Bus4_Selector
module Bus4_Selector (
  input  [3:0] Bus0,
  input  SelectBus,
  input  [3:0] Bus1,
  output [3:0] out_4
);

  Selector Selector0 (.Choice0(Bus0[0]), .select_bit(SelectBus), .Choice1(Bus1[0]), .out_4(out_4[0]));
  Selector Selector1 (.Choice0(Bus0[1]), .select_bit(SelectBus), .Choice1(Bus1[1]), .out_4(out_4[1]));
  Selector Selector2 (.Choice0(Bus0[2]), .select_bit(SelectBus), .Choice1(Bus1[2]), .out_4(out_4[2]));
  Selector Selector3 (.Choice0(Bus0[3]), .select_bit(SelectBus), .Choice1(Bus1[3]), .out_4(out_4[3]));
endmodule

module Selector (
  input  Choice0,
  input  select_bit,
  input  Choice1,
  output out_4
);

  wire and_1_out, and_2_out, not_1_out;

  not not_1 (not_1_out, select_bit);
  and and_1 (and_1_out, Choice0, not_1_out);
  and and_2 (and_2_out, select_bit, Choice1);
  or or_1 (out_4, and_1_out, and_2_out);
endmodule
