// Logisim project Lab2_PartB_forPartC_Casper.circ as structural Verilog: 2 circuits, main circuit Full_Adder
module Full_Adder (
  input  X,
  input  Y,
  input  C_in,
  output S,
  output C_Out
);

  wire and_1_out, and_2_out, xor_1_out;

  xor xor_1 (xor_1_out, X, Y);
  and and_1 (and_1_out, X, Y);
  and and_2 (and_2_out, xor_1_out, C_in);
  xor xor_2 (S, xor_1_out, C_in);
  or or_1 (C_Out, and_2_out, and_1_out);
endmodule

module Bus4BitFullAdder (
  input  SubtractorCarry,
  input  [3:0] Bus1,
  input  [3:0] Bus2,
  output [3:0] out_4
);

  wire Index0Adder_c_out, Index1Adder_c_out, Index2Adder_c_out, xor_1_out, xor_2_out, xor_3_out, xor_4_out;

  xor xor_1 (xor_1_out, SubtractorCarry, Bus1[0]);
  xor xor_2 (xor_2_out, SubtractorCarry, Bus1[1]);
  xor xor_3 (xor_3_out, SubtractorCarry, Bus1[2]);
  xor xor_4 (xor_4_out, SubtractorCarry, Bus1[3]);
  Full_Adder Index0Adder (.X(xor_1_out), .Y(Bus2[0]), .C_in(SubtractorCarry), .S(out_4[0]), .C_Out(Index0Adder_c_out));
  Full_Adder Index1Adder (
    .X(xor_2_out), .Y(Bus2[1]), .C_in(Index0Adder_c_out), .S(out_4[1]), .C_Out(Index1Adder_c_out));
  Full_Adder Index2Adder (
    .X(xor_3_out), .Y(Bus2[2]), .C_in(Index1Adder_c_out), .S(out_4[2]), .C_Out(Index2Adder_c_out));
  Full_Adder Index3Adder (.X(xor_4_out), .Y(Bus2[3]), .C_in(Index2Adder_c_out), .S(out_4[3]));  // open: C_Out
endmodule
