// Logisim project Lab2_PartC.circ as structural Verilog: 4 circuits, main circuit ALU
module ALU (
  input  [3:0] Y,
  input  [1:0] func,
  input  [3:0] X,
  output [3:0] Z
);

  wire [3:0] bus4_selector_1_out_4, bus4and_1_andout, bus4bitfulladder_1_out_4, bus4or_1_orout;

  Bus4BitFullAdder bus4bitfulladder_1 (.SubtractorCarry(func[0]), .Bus1(Y), .Bus2(X), .out_4(bus4bitfulladder_1_out_4));
  Bus4AND bus4and_1 (.X(Y), .Y(X), .AndOut(bus4and_1_andout));
  Bus4OR bus4or_1 (.X(Y), .Y(X), .OrOut(bus4or_1_orout));
  Bus4_Selector bus4_selector_1 (
    .Bus0(bus4and_1_andout), .SelectBus(func[0]), .Bus1(bus4or_1_orout), .out_4(bus4_selector_1_out_4));
  Bus4_Selector bus4_selector_2 (
    .Bus0(bus4bitfulladder_1_out_4), .SelectBus(func[1]), .Bus1(bus4_selector_1_out_4), .out_4(Z));
endmodule

module Bus4AND (
  input  [3:0] X,
  input  [3:0] Y,
  output [3:0] AndOut
);

  and and_1 (AndOut[0], X[0], Y[0]);
  and and_2 (AndOut[1], X[1], Y[1]);
  and and_3 (AndOut[2], Y[2], X[2]);
  and and_4 (AndOut[3], X[3], Y[3]);
endmodule

module Bus4OR (
  input  [3:0] X,
  input  [3:0] Y,
  output [3:0] OrOut
);

  or or_1 (OrOut[0], X[0], Y[0]);
  or or_2 (OrOut[1], X[1], Y[1]);
  or or_3 (OrOut[2], X[2], Y[2]);
  or or_4 (OrOut[3], X[3], Y[3]);
endmodule

module UserCircuit (
  output [3:0] out_1
);

  wire [1:0] dipswitch_1_p1;
  wire [3:0] X_in_p1, Y_in_p1;

  // DipSwitch #(.number(4)) X_in: pin names not known; wires that end beside it: X_in_p1[0], X_in_p1[1], X_in_p1[2], X_in_p1[3]
  // DipSwitch #(.number(4)) Y_in: pin names not known; wires that end beside it: Y_in_p1[0], Y_in_p1[1], Y_in_p1[2], Y_in_p1[3]
  LED led_1 (.in(dipswitch_1_p1[0]));
  // DipSwitch #(.number(2)) dipswitch_1: pin names not known; wires that end beside it: dipswitch_1_p1[0], dipswitch_1_p1[1]
  LED led_2 (.in(dipswitch_1_p1[1]));
  Hex_Digit_Display hex_digit_display_1 (.value(X_in_p1));  // open: dp
  Hex_Digit_Display hex_digit_display_2 (.value(Y_in_p1));  // open: dp
  ALU alu_1 (.Y(X_in_p1), .func(dipswitch_1_p1), .X(Y_in_p1), .Z(out_1));
  Hex_Digit_Display hex_digit_display_3 (.value(out_1));  // open: dp
endmodule
